# Fritzing sketch PrinterBrailleSketch (saved by Fritzing 0.9.3b)

parts:
  Composant1 = Adafruit Motor/Stepper/Servo Shield [part_number="Adafruit #1438"]
  M1 = Stepper Motor - Bipolar
  L1 = Solenoid
  R1 = Resistor [tolerance=±5% resistance=2.2k package=THT]
  D1 = Rectifier Diode [part_number=1N4001 package="300 mil [THT]"]
  Q1 = TIP120 Hi-Current Darlington Transistor
  M2 = Stepper Motor - Bipolar
  S2 = Pushbutton [package=THT]
  Power_plug1 = Power plug

nets:
  N1: Composant1.D2, R1.Pin_0
  N2: Composant1.M2A, M2.A
  N3: Composant1.M2B, M2.C
  N4: Composant1.M1B, M2.B
  N5: Composant1.M1A, M2.D
  N6: Composant1.M3A, M1.D
  N7: Composant1.M3B, M1.B
  N8: Composant1.M4B, M1.C
  N9: Composant1.M4A, M1.A
  GND: Composant1.GND, Q1.EMITTER, S2.leg1, Power_plug1.GND
  N10: Composant1.VMOTOR, L1.pin2, D1.cathode, Power_plug1.VCC
  N11: Composant1.D10, S2.leg0
  N12: L1.pin1, D1.anode, Q1.COLLECTOR
  N13: R1.Pin_1, Q1.BASE

custom parts:
  Adafruit Motor/Stepper/Servo Shield: The original Adafruit Motorshield kit is one of our most beloved kits, which is why we decided to make something even better. We have upgraded the shield kit to make the bestest, easiest way to drive DC and Stepper motors. This shield will make quick work of your next robotics project! We kept the ability to drive up to 4 DC motors or 2 stepper motors, but added many improvements: Instead of a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
